# Fritzing sketch Meteostanice (saved by Fritzing 0.9.3b)
breadboards: 1

parts:
  U2 = ESP32S-HiLetgo [part_number=ESP32S-HiLetgo]
  Q1 = NPN-Transistor [package="TO92 [THT]"]
  Mod1 = CJMCU-811
  BMP280_Breakout2 = BMP280 Breakout Board [part_number=BMP280]
  YL-83_-_Detection_Board2 = YL-83 Rain Sensor - Detection Board
  YL-83_-_Control_Board2 = YL-83 Rain Sensor - Control Board
  SW-2 = Vibration sensor module

nets:
  VCC: U2.3.3, Mod1.VCC, BMP280_Breakout2.VCC, YL-83_-_Control_Board2.VCC, SW-2.vcc
  N1: U2.EN, SW-2.Digital_output
  N2: U2.GPIO34, YL-83_-_Control_Board2.DO
  N3: U2.GND, Q1.E, SW-2.Ground
  N4: U2.GPIO5, Q1.B
  N5: U2.GPIO21, BMP280_Breakout2.SDA
  N6: U2.GPIO22, BMP280_Breakout2.SCL
  GND: Q1.C, Mod1.GND, Mod1.WAK, BMP280_Breakout2.GND, YL-83_-_Control_Board2.GND
  N7: YL-83_-_Detection_Board2.POS, YL-83_-_Control_Board2.POS
  N8: YL-83_-_Detection_Board2.NEG, YL-83_-_Control_Board2.NEG

notes:
  Senzor otřesu
  Senzor deště
  BMP280
  CJMCU-811
  Porty jsou obráceně:
  D0
  GND
  VCC
  Porty jsou obráceně:
  SDA SCL GND VIN

custom parts:
  ESP32S-HiLetgo: HiLetgo ESP-WROOM-32 ESP32 ESP-32S Development Board 2.4GHz Dual-Mode WiFi + Bluetooth Dual Cores Microcontroller The ESP32 integrated with Antenna switches, RF Balun, power amplifiers, low-noise amplifiers, filters, and management modules, and the entire solution occupies the least area of PCB. 2.4 GHz Wi-Fi plus Bluetooth dual-mode chip, with TSMC Ultra-low power consumption 40nm technology,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
  CJMCU-811: The CCS811 is an ultra-low power digital gas sensor solution which integrates a metal oxide (MOX) gas sensor to detect a wide range of Volatile Organic Compounds (VOCs) for indoor air quality monitoring with a microcontroller unit (MCU), which includes an Analog-to-Digital converter (ADC), and an I²C interface.
  BMP280 Breakout Board: This is a breakout board for the Bosch Sensortec BMP280, "an absolute barometric pressure sensor especially designed for mobile applications." The operation range is 300 to 1100 hPa. Supply voltage is 1.2 to 3.6V. Operating temperature range is -40 to +85 °C.
  YL-83 Rain Sensor - Detection Board: The YL-83 is a rain sensor that has more resistance when dry and less resistance when wet. The module runs at 5V.
  YL-83 Rain Sensor - Control Board: The YL-83 is a rain sensor that has more resistance when dry and less resistance when wet. The module runs at 5V.
  Vibration sensor module: Single-roller type full induction trigger switch. When no vibration or tilt, the product is ON conduction state, and in the steady state, when a vibration or tilt, the switch will be rendered instantly disconnect the conductive resistance increases, generating a current pulse signal, thereby triggering circuit. The default state of the swith is close Digital output Supply voltage:3.3V-5V On-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
